# Fritzing sketch New_board3 (saved by Fritzing 0.9.3b)
circuit board: 14.5148cm x 5.9872cm
breadboards: 1

parts:
  U1 = V_REG_LD1117VXX [package=78xxl]
  C1 = Ceramic Capacitor [capacitance=100nF voltage=5.5V package="100 mil [THT, multilayer]"]
  C2 = Electrolytic Capacitor [capacitance=10µF package="100 mil [THT, electrolytic]"]
  S1 = Pushbutton [package="[THT]"]
  S2 = Pushbutton [package="[THT]"]
  S3 = Pushbutton [package="[THT]"]
  S4 = Pushbutton [package="[THT]"]
  S5 = Pushbutton [package="[THT]"]
  S6 = Toggle Switch [package=THT]
  S7 = Toggle Switch [package=THT]
  LED1 = LED - 5mm [color="Red (635nm)" package="5 mm [THT]"]
  LED2 = LED - 5mm [color="Yellow (585nm)" package="5 mm [THT]"]
  LED3 = LED - 5mm [color="Green (565nm)" package="5 mm [THT]"]
  LED4 = LED - 5mm [color="Blue (430nm)" package="5 mm [THT]"]
  R1 = Resistor [tolerance=±5% resistance=35 package=THT]
  R2 = Resistor [tolerance=±5% resistance=25 package=THT]
  R3 = Resistor [tolerance=±5% resistance=35 package=THT]
  R4 = Resistor [tolerance=±5% resistance=85 package=THT]
  J1 = Raspberry PI B 40-pin header [form="♂ (shrouded male)" package=THT]
  R21 = Resistor [tolerance=±5% resistance=2.2k package=THT]
  R22 = Resistor [tolerance=±5% resistance=680 package=THT]
  Q1 = NPN-Transistor [package="TO92 [THT]"]
  IC1 = Hex Inverter Schmitt Trigger SN74HC14 [package="DIP (Dual Inline)"]
  IC2 = Hex Inverter Schmitt Trigger SN74HC14 [package="DIP (Dual Inline)"]
  R1_2 = Resistor [tolerance=±5% resistance=47k package=THT]
  D1 = Rectifier Diode [part_number=1N4001 package="300 mil [THT]"]
  R2_2 = Resistor [tolerance=±5% resistance=47k package=THT]
  C3 = Electrolytic Capacitor [capacitance=1µF package="100 mil [THT, electrolytic]"]
  R23 = Resistor [tolerance=±5% resistance=47k package=THT]
  R24 = Resistor [tolerance=±5% resistance=47k package=THT]
  D2 = Rectifier Diode [part_number=1N4001 package="300 mil [THT]"]
  C4 = Electrolytic Capacitor [capacitance=1µF package="100 mil [THT, electrolytic]"]
  R25 = Resistor [tolerance=±5% resistance=47k package=THT]
  R26 = Resistor [tolerance=±5% resistance=47k package=THT]
  D3 = Rectifier Diode [part_number=1N4001 package="300 mil [THT]"]
  C5 = Electrolytic Capacitor [capacitance=1µF package="100 mil [THT, electrolytic]"]
  R27 = Resistor [tolerance=±5% resistance=47k package=THT]
  R28 = Resistor [tolerance=±5% resistance=47k package=THT]
  D4 = Rectifier Diode [part_number=1N4001 package="300 mil [THT]"]
  C6 = Electrolytic Capacitor [capacitance=1µF package="100 mil [THT, electrolytic]"]
  R29 = Resistor [tolerance=±5% resistance=47k package=THT]
  R30 = Resistor [tolerance=±5% resistance=47k package=THT]
  D5 = Rectifier Diode [part_number=1N4001 package="300 mil [THT]"]
  C7 = Electrolytic Capacitor [capacitance=1µF package="100 mil [THT, electrolytic]"]
  R31 = Resistor [tolerance=±5% resistance=47k package=THT]
  R32 = Resistor [tolerance=±5% resistance=47k package=THT]
  D6 = Rectifier Diode [part_number=1N4001 package="300 mil [THT]"]
  C8 = Electrolytic Capacitor [capacitance=1µF package="100 mil [THT, electrolytic]"]
  R33 = Resistor [tolerance=±5% resistance=47k package=THT]
  R34 = Resistor [tolerance=±5% resistance=47k package=THT]
  D7 = Rectifier Diode [part_number=1N4001 package="300 mil [THT]"]
  C9 = Electrolytic Capacitor [capacitance=1µF package="100 mil [THT, electrolytic]"]
  R35 = Resistor [tolerance=±5% resistance=1k package=THT]
  R36 = Resistor [tolerance=±5% resistance=10k package=THT]
  R37 = Resistor [tolerance=±5% resistance=1k package=THT]
  R38 = Resistor [tolerance=±5% resistance=10k package=THT]
  R39 = Resistor [tolerance=±5% resistance=1k package=THT]
  R40 = Resistor [tolerance=±5% resistance=10k package=THT]
  R41 = Resistor [tolerance=±5% resistance=1k package=THT]
  R42 = Resistor [tolerance=±5% resistance=10k package=THT]
  R43 = Resistor [tolerance=±5% resistance=1k package=THT]
  R44 = Resistor [tolerance=±5% resistance=10k package=THT]
  R45 = Resistor [tolerance=±5% resistance=1k package=THT]
  R46 = Resistor [tolerance=±5% resistance=10k package=THT]
  R47 = Resistor [tolerance=±5% resistance=1k package=THT]
  R48 = Resistor [tolerance=±5% resistance=10k package=THT]

nets:
  N1: U1.OUT, C2.+, R1_2.Pin_1, R23.Pin_1, R26.Pin_1, R28.Pin_1, R30.Pin_1, R32.Pin_1, R34.Pin_1
  GND: U1.GND, C1.0, C2.-, S1.Pin_4, S2.Pin_3, S2.Pin_4, S3.Pin_3, S3.Pin_4, S4.Pin_3, S4.Pin_4, S5.Pin_3, S5.Pin_4, S6.L1, S7.L1, J1.Pin_9, J1.Pin_39, J1.Pin_30, J1.Pin_20, J1.Pin_6, R22.Pin_1, Q1.E, IC1.GND, IC1.4A, IC1.5A, IC1.6A, IC2.GND, IC2.5A, IC2.6A, C3.-, C4.-, C5.-, C6.-, C7.-, C8.-, C9.-, R36.Pin_0, R38.Pin_0, R40.Pin_0, R42.Pin_0, R44.Pin_0, R46.Pin_0, R48.Pin_0
  N2: U1.IN, C1.1, J1.Pin_4, J1.Pin_2
  N3: S1.Pin_1, S1.Pin_2, IC1.1A, R1_2.Pin_0, D1.anode, R2_2.Pin_1
  N4: S2.Pin_1, S2.Pin_2, IC1.2A, R23.Pin_0, R24.Pin_1, D2.anode
  N5: S3.Pin_1, S3.Pin_2, IC1.3A, R25.Pin_1, R26.Pin_0, D3.anode
  N6: S4.Pin_1, S4.Pin_2, IC2.1A, R27.Pin_1, R28.Pin_0, D4.anode
  N7: S5.Pin_1, S5.Pin_2, IC2.2A, R29.Pin_1, R30.Pin_0, D5.anode
  N8: S6.COM, IC2.3A, R31.Pin_1, R32.Pin_0, D6.anode
  N9: S7.COM, IC2.4A, R33.Pin_1, R34.Pin_0, D7.anode
  N10: LED1.cathode, R1.Pin_1
  N11: LED2.cathode, R2.Pin_1
  N12: LED3.cathode, R3.Pin_1
  N13: LED4.cathode, R4.Pin_1
  N14: R1.Pin_0, Q1.C
  N15: J1.Pin_3, R37.Pin_0
  N16: J1.Pin_5, R41.Pin_0
  N17: J1.Pin_7, R43.Pin_0
  N18: J1.Pin_27, R35.Pin_0
  N19: J1.Pin_29, R45.Pin_0
  N20: J1.Pin_31, R47.Pin_0
  N21: J1.Pin_28, R39.Pin_0
  N22: J1.Pin_26, R21.Pin_0
  N23: R21.Pin_1, R22.Pin_0, Q1.B
  N24: IC1.1Y, R35.Pin_1, R36.Pin_1
  N25: IC1.2Y, R39.Pin_1, R40.Pin_1
  N26: IC1.3Y, R37.Pin_1, R38.Pin_1
  N27: IC2.1Y, R41.Pin_1, R42.Pin_1
  N28: IC2.2Y, R43.Pin_1, R44.Pin_1
  N29: IC2.3Y, R45.Pin_1, R46.Pin_1
  N30: IC2.4Y, R47.Pin_1, R48.Pin_1
  N31: D1.cathode, R2_2.Pin_0, C3.+
  N32: R24.Pin_0, D2.cathode, C4.+
  N33: R25.Pin_0, D3.cathode, C5.+
  N34: R27.Pin_0, D4.cathode, C6.+
  N35: R29.Pin_0, D5.cathode, C7.+
  N36: R31.Pin_0, D6.cathode, C8.+
  N37: R33.Pin_0, D7.cathode, C9.+

notes:
  800mA out
  make pullup/down external?
  3.3V 50mA is shared amongst ALL pins
  Blue LED needs 5V!
  RC debounce ROUGHLY
  C = 1uF
  R1+R2 = 80K
  delay time ~ 24ms
  at 3.3V
  with diode 35975
  feed trigger 74HC14

custom parts:
  Raspberry PI B 40-pin header: 40-pin header for the PI 3 model B
