# Fritzing sketch New_board4 (saved by Fritzing 0.9.3b)
circuit board: 12.2406cm x 7.35526cm
breadboards: 1

parts:
  U1 = V_REG_LD1117VXX [package=78xxl]
  C1 = Ceramic Capacitor [capacitance=100nF voltage=5.5V package="100 mil [THT, multilayer]"]
  C2 = Electrolytic Capacitor [capacitance=10µF package="100 mil [THT, electrolytic]"]
  S1 = Pushbutton [package="[THT]"]
  S2 = Pushbutton [package="[THT]"]
  S3 = Pushbutton [package="[THT]"]
  S4 = Pushbutton [package="[THT]"]
  S5 = Pushbutton [package="[THT]"]
  S6 = Toggle Switch [package=THT]
  S7 = Toggle Switch [package=THT]
  LED1 = LED - 5mm [color="Red (635nm)" package="5 mm [THT]"]
  LED2 = LED - 5mm [color="Yellow (585nm)" package="5 mm [THT]"]
  LED3 = LED - 5mm [color="Green (565nm)" package="5 mm [THT]"]
  LED4 = LED - 5mm [color="Blue (430nm)" package="5 mm [THT]"]
  R1 = Resistor [tolerance=±5% resistance=35 package=THT]
  R2 = Resistor [tolerance=±5% resistance=25 package=THT]
  R3 = Resistor [tolerance=±5% resistance=35 package=THT]
  R4 = Resistor [tolerance=±5% resistance=85 package=THT]
  J1 = Raspberry PI B 40-pin header [form="♂ (shrouded male)" package=THT]
  R21 = Resistor [tolerance=±5% resistance=2.2k package=THT]
  Q1 = NPN-Transistor [package="TO92 [THT]"]
  IC1 = Hex Inverter Schmitt Trigger SN74HC14 [package="DIP (Dual Inline)"]
  R1_2 = Resistor [tolerance=±5% resistance=47k package=THT]
  D1 = Rectifier Diode [part_number=1N4001 package="300 mil [THT]"]
  R2_2 = Resistor [tolerance=±5% resistance=47k package=THT]
  C3 = Electrolytic Capacitor [capacitance=1µF package="100 mil [THT, electrolytic]"]
  R23 = Resistor [tolerance=±5% resistance=47k package=THT]
  R24 = Resistor [tolerance=±5% resistance=47k package=THT]
  D2 = Rectifier Diode [part_number=1N4001 package="300 mil [THT]"]
  C4 = Electrolytic Capacitor [capacitance=1µF package="100 mil [THT, electrolytic]"]
  R25 = Resistor [tolerance=±5% resistance=47k package=THT]
  R26 = Resistor [tolerance=±5% resistance=47k package=THT]
  D3 = Rectifier Diode [part_number=1N4001 package="300 mil [THT]"]
  C5 = Electrolytic Capacitor [capacitance=1µF package="100 mil [THT, electrolytic]"]
  R27 = Resistor [tolerance=±5% resistance=47k package=THT]
  R28 = Resistor [tolerance=±5% resistance=47k package=THT]
  D4 = Rectifier Diode [part_number=1N4001 package="300 mil [THT]"]
  C6 = Electrolytic Capacitor [capacitance=1µF package="100 mil [THT, electrolytic]"]
  R29 = Resistor [tolerance=±5% resistance=47k package=THT]
  R30 = Resistor [tolerance=±5% resistance=47k package=THT]
  D5 = Rectifier Diode [part_number=1N4001 package="300 mil [THT]"]
  C7 = Electrolytic Capacitor [capacitance=1µF package="100 mil [THT, electrolytic]"]
  R35 = Resistor [tolerance=±5% resistance=150k package=THT]
  R38 = Resistor [tolerance=±5% resistance=2.2k package=THT]
  Q3 = NPN-Transistor [package="TO92 [THT]"]
  R40 = Resistor [tolerance=±5% resistance=2.2k package=THT]
  Q4 = NPN-Transistor [package="TO92 [THT]"]
  R42 = Resistor [tolerance=±5% resistance=2.2k package=THT]
  Q5 = NPN-Transistor [package="TO92 [THT]"]
  7_Segment1 = 7 Segment Display
  IC3 = IC, DIP package, 16 pins [chip_label=IC]
  R49 = Resistor [tolerance=±5% resistance=220k package=THT]
  R50 = Resistor [tolerance=±5% resistance=220k package=THT]
  R52 = Resistor [tolerance=±5% resistance=220k package=THT]
  R51 = Resistor [tolerance=±5% resistance=220k package=THT]
  R53 = Resistor [tolerance=±5% resistance=150k package=THT]
  IC7 = 4011 4 x 2 Input NAND Gate, single part [part_number=4011 package="DIP (Dual Inline) [THT]"]
  R55 = Resistor [tolerance=±5% resistance=150k package=THT]
  Part1 = Adafruit ADS1115 16Bit I2C ADC [part_number="Adafruit #1085"]
  T1 = TMP36 Temperature Sensor [package="TO92 [THT]"]
  J2 = Piezo Speaker
  R56 = Resistor [tolerance=±5% resistance=47k package=THT]
  Q6 = LTR-301 [package=ltr-301]
  R57 = Resistor [tolerance=±5% resistance=2.2k package=THT]
  I2C = male pin header, 4 pins [form="♂ (male)"]
  ADC = male pin header, 4 pins [form="♂ (male)"]
  UART = male pin header, 4 pins [form="♂ (male)"]
  ADC_ATTACH = male pin header, 10 pins [form="♂ (male)"]
  Q7 = NPN-Transistor [package="TO92 [THT]"]
  R58 = Resistor [tolerance=±5% resistance=2.2k package=THT]
  R59 = Resistor [tolerance=±5% resistance=2.2k package=THT]
  R60 = Resistor [tolerance=±5% resistance=68 package=THT]
  R61 = Resistor [tolerance=±5% resistance=68 package=THT]
  R62 = Resistor [tolerance=±5% resistance=68 package=THT]
  R63 = Resistor [tolerance=±5% resistance=68 package=THT]
  R64 = Resistor [tolerance=±5% resistance=68 package=THT]
  R65 = Resistor [tolerance=±5% resistance=68 package=THT]
  R66 = Resistor [tolerance=±5% resistance=68 package=THT]

nets:
  3.3V: U1.OUT, C2.+, LED1.anode, LED2.anode, LED3.anode, R1_2.Pin_1, R23.Pin_1, R26.Pin_1, R28.Pin_1, R30.Pin_1, R35.Pin_1, IC3.pin16, R49.Pin_1, R50.Pin_1, R52.Pin_1, R51.Pin_1, R53.Pin_1, R55.Pin_1, Part1.VDD, R56.Pin_0, Q6.C, I2C.pin1, ADC.pin1, UART.pin1, ADC_ATTACH.pin1, R59.Pin_0
  GND: U1.GND, C1.0, C2.-, S1.Pin_3, S1.Pin_4, S2.Pin_3, S2.Pin_4, S3.Pin_3, S3.Pin_4, S4.Pin_3, S4.Pin_4, S5.Pin_3, S5.Pin_4, S6.COM, S7.COM, J1.Pin_9, J1.Pin_25, J1.Pin_39, J1.Pin_30, J1.Pin_14, J1.Pin_6, Q1.E, IC1.GND, IC1.6A, C3.-, C4.-, C5.-, C6.-, C7.-, Q3.E, Q4.E, Q5.E, 7_Segment1.common_cathode, IC3.pin5, IC3.pin8, IC7.GND, Part1.ADDR, Part1.GND, T1.GND, R57.Pin_0, I2C.pin4, ADC.pin4, UART.pin4, ADC_ATTACH.pin2, ADC_ATTACH.pin5, Q7.E
  N1: U1.IN, C1.1, LED4.anode, J1.Pin_4, J1.Pin_2
  N2: S1.Pin_1, S1.Pin_2, IC1.1A, R1_2.Pin_0, D1.anode, R2_2.Pin_1
  N3: S2.Pin_1, S2.Pin_2, IC1.2A, R23.Pin_0, R24.Pin_1, D2.anode
  N4: S3.Pin_1, S3.Pin_2, IC1.3A, R25.Pin_1, R26.Pin_0, D3.anode
  N5: S4.Pin_1, S4.Pin_2, IC1.4A, R27.Pin_1, R28.Pin_0, D4.anode
  N6: S5.Pin_1, S5.Pin_2, IC1.5A, R29.Pin_1, R30.Pin_0, D5.anode
  N7: S6.L1, R49.Pin_0, IC7.B1
  N8: S6.L2, R50.Pin_0, IC7.B2
  N9: S7.L1, R51.Pin_0, IC7.B4
  N10: S7.L2, R52.Pin_0, IC7.A3
  N11: LED1.cathode, R1.Pin_1
  N12: LED2.cathode, R2.Pin_1
  N13: LED3.cathode, R3.Pin_1
  N14: LED4.cathode, R4.Pin_1
  N15: R1.Pin_0, Q1.C
  N16: R2.Pin_0, Q3.C
  N17: R3.Pin_0, Q4.C
  N18: R4.Pin_0, Q5.C
  N19: J1.Pin_3, Part1.SDA, I2C.pin2, ADC_ATTACH.pin4
  N20: J1.Pin_5, Part1.SCL, I2C.pin3, ADC_ATTACH.pin3
  N21: J1.Pin_7, Part1.ALERT, ADC_ATTACH.pin6
  N22: J1.Pin_11, R42.Pin_0
  N23: J1.Pin_15, IC3.pin1
  N24: J1.Pin_19, IC7.A1, IC7.Q2
  N25: J1.Pin_21, IC1.5Y
  N26: J1.Pin_23, IC7.B3, IC7.Q4
  N27: J1.Pin_29, IC1.1Y
  N28: J1.Pin_31, IC1.2Y
  N29: J1.Pin_33, R38.Pin_0
  N30: J1.Pin_35, IC3.pin4
  N31: J1.Pin_40, IC3.pin2
  N32: J1.Pin_38, IC3.pin6
  N33: J1.Pin_36, R40.Pin_0
  N34: J1.Pin_32, R21.Pin_0
  N35: J1.Pin_26, IC1.3Y
  N36: J1.Pin_24, IC1.4Y
  N37: J1.Pin_16, IC3.pin7
  N38: J1.Pin_12, R58.Pin_0
  N39: J1.Pin_10, UART.pin3
  N40: J1.Pin_8, UART.pin2
  N41: R21.Pin_1, Q1.B
  N42: IC1.VCC, R35.Pin_0
  N43: D1.cathode, R2_2.Pin_0, C3.+
  N44: R24.Pin_0, D2.cathode, C4.+
  N45: R25.Pin_0, D3.cathode, C5.+
  N46: R27.Pin_0, D4.cathode, C6.+
  N47: R29.Pin_0, D5.cathode, C7.+
  N48: R38.Pin_1, Q3.B
  N49: R40.Pin_1, Q4.B
  N50: R42.Pin_1, Q5.B
  N51: 7_Segment1.Segment_E, R64.Pin_1
  N52: 7_Segment1.Segment_D, R63.Pin_1
  N53: 7_Segment1.Segment_C, R62.Pin_1
  N54: 7_Segment1.Segment_B, R61.Pin_1
  N55: 7_Segment1.Segment_A, R60.Pin_1
  N56: 7_Segment1.Segment_F, R65.Pin_1
  N57: 7_Segment1.Segment_G, R66.Pin_1
  N58: IC3.pin3, R55.Pin_0
  N59: IC3.pin9, R64.Pin_0
  N60: IC3.pin10, R63.Pin_0
  N61: IC3.pin11, R62.Pin_0
  N62: IC3.pin12, R61.Pin_0
  N63: IC3.pin13, R60.Pin_0
  N64: IC3.pin14, R66.Pin_0
  N65: IC3.pin15, R65.Pin_0
  N66: R53.Pin_0, IC7.VDD
  N67: IC7.Q1, IC7.A2
  N68: IC7.Q3, IC7.A4
  N69: Part1.AIN3, ADC.pin3, ADC_ATTACH.pin10
  N70: Part1.AIN2, ADC.pin2, ADC_ATTACH.pin9
  N71: Part1.AIN1, Q6.E, R57.Pin_1, ADC_ATTACH.pin8
  N72: Part1.AIN0, T1.Vout, ADC_ATTACH.pin7
  N73: T1.+Vs, R56.Pin_1
  N74: J2.pin1, R59.Pin_1
  N75: J2.pin2, Q7.C
  N76: Q7.B, R58.Pin_1

notes:
  800mA out
  3.3V 50mA is shared amongst ALL pins
  Blue LED needs 5V!
  RC debounce ROUGHLY
  C = 1uF
  R1+R2 = 80K
  delay time ~ 24ms
  at 3.3V
  with diode 35975
  feed trigger 74HC14
  ?????
  Resistors to pins!
  Need to get measurements
  Tie GPCLK0 to the red LED as well? Speaker? TOGGLE SWITCH???
  UART
  3.3V
  TXD
  RXD
  GND
  3.3V
  SDA
  SCL
  GND
  3.3V
  AIN2
  AIN3
  GND
  jumpers next to AINs for gnd?
  ADDR -> GND
  I2C address 0x48
  NO IDEA HOW TO WIRE

custom parts:
  Raspberry PI B 40-pin header: 40-pin header for the PI 3 model B
  Adafruit ADS1115 16Bit I2C ADC: For microcontrollers without an analog-to-digital converter or when you want a higher-precision ADC, the ADS1115 provides 16-bit precision at 860 samples/second over I2C. The chip can be configured as 4 single-ended input channels, or two differential channels. As a nice bonus, it even includes a programmable gain amplifier, up to x16, to help boost up smaller single/differential signals to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
